# Fritzing sketch uno_ct_pm11v (saved by Fritzing 0.9.3b)
circuit board: 6.93142cm x 5.35457cm
breadboards: 1

parts:
  U1 = IC, DIP package, 8 pins [chip_label=TL072]
  C3 = Ceramic Capacitor [capacitance=100nF voltage=35V package="100 mil [THT, multilayer]"]
  R6 = Resistor [tolerance=±5% resistance=10k package=THT]
  R5 = Resistor [tolerance=±5% resistance=39k package=THT]
  R12 = Resistor [tolerance=±5% resistance=9.1k package=THT]
  R1 = Rotary Potentiometer (Small) [maximum_resistance=1kΩ package=THT]
  R3 = Resistor [tolerance=±5% resistance=1k package=THT]
  R7 = Resistor [tolerance=±5% resistance=100k package=THT]
  R4 = Resistor [tolerance=±5% resistance=100k package=THT]
  C1 = Ceramic Capacitor [capacitance=1nF voltage=35V package="100 mil [THT, multilayer]"]
  R10 = Resistor [tolerance=±5% resistance=100k package=THT]
  R9 = Resistor [tolerance=±5% resistance=33k package=THT]
  C2 = Ceramic Capacitor [capacitance=1nF voltage=35V package="100 mil [THT, multilayer]"]
  R13 = Resistor [tolerance=±5% resistance=10k package=THT]
  R8 = Resistor [tolerance=±5% resistance=75k package=THT]
  C4 = Ceramic Capacitor [capacitance=100nF voltage=35V package="100 mil [THT, multilayer]"]
  C5 = Ceramic Capacitor [capacitance=100nF voltage=35V package="100 mil [THT, multilayer]"]
  Part1 = Arduino Uno (Rev3)
  VCC3 = Battery block 9V
  VCC4 = Battery block 9V
  R11 = Resistor [tolerance=±5% resistance=2.2k package=THT]
  C6 = Ceramic Capacitor [capacitance=0.47µF voltage=35V package="100 mil [THT, multilayer]"]
  R14 = Resistor [tolerance=±5% resistance=22k package=THT]
  J1 = female pin header, 3 pins [form="♀ (female)"]
  R15 = Resistor [tolerance=±5% resistance=200k package=THT]
  VCC1 = Battery block 9V
  VCC2 = Battery block 9V
  S1 = Toggle Switch [package=THT]
  S2 = Toggle Switch [package=THT]

nets:
  N1: U1.pin1, R5.Pin_0, R12.Pin_1, R11.Pin_0
  N2: U1.pin2, R5.Pin_1
  N3: U1.pin3, C3.0, R6.Pin_0
  N4: U1.pin4, C4.0, S1.L2
  N5: U1.pin5, U1.pin8, C3.1, R1.leg2, C1.0, C2.0, R8.Pin_1, C4.1, C5.0, C5.1, Part1.GND, VCC4.+, C6.0, VCC1.-, S2.L2
  N6: U1.pin6, R3.Pin_0, J1.pin1
  N7: U1.pin7, R3.Pin_1, R7.Pin_0
  N8: R6.Pin_1, Part1.D3_PWM
  N9: R12.Pin_0, R1.wiper
  N10: R1.leg1, R4.Pin_1, R13.Pin_1, Part1.5V
  N11: R7.Pin_1, R4.Pin_0, C1.1, Part1.A0
  N12: R10.Pin_0, R11.Pin_1, J1.pin2
  N13: R10.Pin_1, R9.Pin_0, C2.1, R8.Pin_0, Part1.A2
  N14: R9.Pin_1, R13.Pin_0
  N15: Part1.D11_PWM/MOSI, R14.Pin_1
  N16: VCC3.-, S1.COM
  N17: VCC3.+, VCC4.-
  N18: C6.1, R14.Pin_0, R15.Pin_1
  N19: J1.pin3, R15.Pin_0
  N20: VCC1.+, VCC2.-
  N21: VCC2.+, S2.COM

notes:
  -18V
  +18V
  GND
  +5V
  CT+
  CT-
  + -
  Ct-
  Step
  Ct+
